# Fritzing sketch Weather station (saved by Fritzing 0.9.3b)

parts:
  WeMos_D1_Mini1 = WeMos D1 Mini
  TTP223B1 = TTP223B Capacitive Touch Sensor Module [part_number="Left button"]
  TTP223B2 = TTP223B Capacitive Touch Sensor Module [part_number="Right button"]
  DS2 = DS18B20 1-Wire Temperature Sensor [part_number=DS18B20]
  J1 = female pin header, 3 pins [form="♀ (female)"]
  J2 = male pin header, 3 pins [form="♂ (male)"]
  DS3 = DS18B20 1-Wire Temperature Sensor [part_number=DS18B20]
  J3 = female pin header, 3 pins [form="♀ (female)"]
  J4 = male pin header, 3 pins [form="♂ (male)"]
  R1 = Resistor [tolerance=±5% resistance=4.7k package="2010 [SMD]"]
  LCD1 = LCD screen
  Q2 = NPN-Transistor [package="TO92 [THT]"]

nets:
  N1: WeMos_D1_Mini1.A0, TTP223B2.SIG
  N2: WeMos_D1_Mini1.D0, Q2.B
  N3: WeMos_D1_Mini1.D1, J1.pin2, J3.pin2
  N4: WeMos_D1_Mini1.D2, TTP223B1.SIG
  N5: WeMos_D1_Mini1.D3, LCD1.E
  N6: WeMos_D1_Mini1.D4, LCD1.RS
  N7: WeMos_D1_Mini1.D5, LCD1.DB7
  N8: WeMos_D1_Mini1.D6, LCD1.DB6
  N9: WeMos_D1_Mini1.D7, LCD1.DB5
  N10: WeMos_D1_Mini1.D8, LCD1.DB4
  N11: DS2.VDD, J2.pin3
  N12: DS2.DQ, J2.pin2
  N13: DS2.GND, J2.pin1
  N14: DS3.VDD, J4.pin3
  N15: DS3.DQ, J4.pin2
  N16: DS3.GND, J4.pin1
  N17: J3.pin3, R1.Pin_1
  N18: LCD1.LED-, Q2.C

custom parts:
  WeMos D1 Mini: The D1 mini is a mini wifi board based on ESP-8266EX.
  TTP223B Capacitive Touch Sensor Module: The TTP223B capacitive touch sensor module uses the TTP223B IC. The appropriate voltage is approximately 2 to 5.5 volts.
